# Fritzing sketch oh_behave (saved by Fritzing 1.0.5)
breadboards: 2

parts:
  A1 = Teensy 4.0
  Part1 = Adafruit MCP4728
  Pre-Assembled_Female_BNC1 = Pre-Assembled Female BNC
  Pre-Assembled_Female_BNC2 = Pre-Assembled Female BNC
  Pre-Assembled_Female_BNC3 = Pre-Assembled Female BNC
  Pre-Assembled_Female_BNC4 = Pre-Assembled Female BNC
  CAPSENSE1 = AT42QT1010 Momentary Capsense Breakout
  R1 = Resistor [tolerance=±5% power=0.25W resistance=2000 package=THT]
  FET1 = STP16NF06 N-Channel Power MOSFET
  FET2 = STP16NF06 N-Channel Power MOSFET
  Pre-Assembled_Female_BNC6 = Pre-Assembled Female BNC
  D1 = Diode [package=diode-hv]
  D2 = Diode [package=diode-hv]
  Pre-Assembled_Female_BNC5 = Pre-Assembled Female BNC
  R2 = Resistor [tolerance=±5% power=0.25W resistance=1000 package=THT]
  CAPSENSE2 = AT42QT1010 Momentary Capsense Breakout
  Power_plug1 = Power plug
  Power_plug2 = Power plug
  R3 = Resistor [tolerance=±5% power=0.25W resistance=1000 package=THT]
  R4 = Resistor [tolerance=±5% power=0.25W resistance=2000 package=THT]

nets (from the breadboard view):
  GND: A1.pin_1, A1.pin_17, A1.pin_32, Part1.GND, Pre-Assembled_Female_BNC1.GND, Pre-Assembled_Female_BNC2.GND, Pre-Assembled_Female_BNC3.GND, Pre-Assembled_Female_BNC4.GND, CAPSENSE1.GND, R1.Pin_0, Pre-Assembled_Female_BNC6.GND, Pre-Assembled_Female_BNC5.GND, CAPSENSE2.GND, Power_plug1.GND, Power_plug2.GND, R4.Pin_0
  N1: A1.pin_6, FET1.gate
  N2: A1.pin_8, FET2.gate
  N3: A1.pin_27, R3.Pin_1, R4.Pin_1
  N4: A1.pin_29, R1.Pin_1, R2.Pin_0
  VDD: Part1.VCC, CAPSENSE1.VDD, CAPSENSE2.VDD
  N5: Part1.VOUTA, Pre-Assembled_Female_BNC1.PRB
  N6: Part1.VOUTB, Pre-Assembled_Female_BNC2.PRB
  N7: Part1.VOUTC, Pre-Assembled_Female_BNC3.PRB
  N8: Part1.VOUTD, Pre-Assembled_Female_BNC4.PRB
  N9: CAPSENSE1.OUT, R2.Pin_1
  N10: FET1.drain, D2.A
  N11: FET1.source, FET2.source, Power_plug2.VCC
  N12: FET2.drain, D1.A
  N13: Pre-Assembled_Female_BNC6.PRB, D1.C
  N14: D2.C, Pre-Assembled_Female_BNC5.PRB
  N15: CAPSENSE2.OUT, R3.Pin_0

custom parts:
  Teensy 4.0: The Teensy is a complete USB-based microcontoller development system, in a very small footprint, capable of implementing many types of projects. All programming is done via the USB port. No special programmer is needed, only a standard micro-USB cable and a PC or Macintosh with a USB port. (Oct 2023 added the VBUS pad at user request.)
  Adafruit MCP4728: If you've ever said to yourself "Gee, I wish these four 12-bit DACs came in a single package with the ability to save their settings to an EEPROM", well I have good news. The MCP4728 is the answer to your wishes! Within it's little package, the MCP4728 has four, count em, four 12-bit DACs for whatever voltage setting needs you may have. In addition, it has the ability to store the settings for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
  AT42QT1010 Momentary Capsense Breakout: A capacitive touch momentary switch breakout for the AT42QT1010 chip.
  STP16NF06 N-Channel Power MOSFET: STP16NF06 N-channel Power MOSFET
